// Logisim project MIDTERM PROJECT.circ as structural Verilog: 12 circuits, main circuit main
module main (
  input  S1,
  input  S2,
  input  C1,
  output out_4,
  output out_5,
  output out_6,
  output out_7,
  output out_8,
  output out_9,
  output out_10
);

  a a_1 (.A(S1), .B(S2), .C(C1), .out_4(out_4));
  b b_1 (.A(S1), .B(S2), .C(C1), .out_4(out_5));
  c c_1 (.A(S1), .B(S2), .C(C1), .out_4(out_6));
  d d_1 (.A(S1), .B(S2), .C(C1), .out_4(out_7));
  e e_1 (.A(S1), .B(S2), .C(C1), .out_4(out_8));
  f f_1 (.A(S1), .B(S2), .C(C1), .out_4(out_9));
  g g_1 (.A(S1), .B(S2), .C(C1), .out_4(out_10));
endmodule

module a (
  input  A,
  input  B,
  input  C,
  output out_4
);

  wire and_1_out, and_2_out, not_1_out, not_2_out;

  not not_1 (not_1_out, A);
  not not_2 (not_2_out, C);
  and and_1 (and_1_out, not_1_out, not_2_out);
  and and_2 (and_2_out, A, C);
  or or_1 (out_4, and_1_out, and_2_out, B);
endmodule

module b (
  input  A,
  input  B,
  input  C,
  output out_4
);

  wire and_1_out, and_2_out, not_1_out, not_2_out, not_3_out;

  not not_1 (not_1_out, A);
  not not_2 (not_2_out, B);
  not not_3 (not_3_out, C);
  and and_1 (and_1_out, B, C);
  and and_2 (and_2_out, not_2_out, not_3_out);
  or or_1 (out_4, not_1_out, and_1_out, and_2_out);
endmodule

module c (
  input  A,
  input  B,
  input  C,
  output out_4
);

  wire not_1_out;

  not not_1 (not_1_out, B);
  or or_1 (out_4, A, not_1_out, C);
endmodule

module d (
  input  A,
  input  B,
  input  C,
  output out_4
);

  wire and_1_out, and_2_out, and_3_out, and_4_out, not_1_out, not_2_out, not_3_out, not_4_out;

  not not_1 (not_1_out, B);
  not not_2 (not_2_out, A);
  not not_3 (not_3_out, C);
  not not_4 (not_4_out, C);
  and and_1 (and_1_out, A, not_1_out, C);
  and and_2 (and_2_out, not_2_out, not_3_out);
  and and_3 (and_3_out, not_2_out, B);
  and and_4 (and_4_out, B, not_4_out);
  or or_1 (out_4, and_1_out, and_2_out, and_3_out, and_4_out);
endmodule

module e (
  input  A,
  input  B,
  input  C,
  output out_4
);

  wire and_1_out, and_2_out, not_1_out, not_2_out, not_3_out;

  not not_1 (not_1_out, A);
  not not_2 (not_2_out, C);
  not not_3 (not_3_out, C);
  and and_1 (and_1_out, not_1_out, not_1_out, not_2_out);
  and and_2 (and_2_out, B, not_3_out);
  or or_1 (out_4, and_1_out, and_2_out);
endmodule

module f (
  input  A,
  input  B,
  input  C,
  output out_4
);

  wire and_1_out, and_2_out, and_3_out, not_1_out, not_2_out;

  not not_1 (not_1_out, B);
  not not_2 (not_2_out, C);
  and and_1 (and_1_out, A, not_2_out);
  and and_2 (and_2_out, A, not_1_out);
  and and_3 (and_3_out, not_1_out, not_2_out);
  or or_1 (out_4, and_1_out, and_2_out, and_3_out);
endmodule

module g (
  input  A,
  input  B,
  input  C,
  output out_4
);

  wire and_1_out, and_2_out, and_3_out, not_1_out, not_2_out, not_3_out;

  not not_1 (not_1_out, B);
  not not_2 (not_2_out, A);
  not not_3 (not_3_out, C);
  and and_1 (and_1_out, A, not_1_out);
  and and_2 (and_2_out, not_2_out, B);
  and and_3 (and_3_out, A, not_3_out);
  or or_1 (out_4, and_1_out, and_2_out, and_3_out);
endmodule

module _7_Segment_Display (
  input  in_1,
  input  in_2,
  input  in_3,
  input  in_4,
  input  in_5,
  input  in_6,
  input  in_7,
  input  in_8
);

  _7_Segment_Display_part u_7_segment_display_1 (
    .g(in_4), .f(in_3), .a(in_2), .b(in_1), .e(in_5), .d(in_6), .c(in_7), .dp(in_8));
endmodule

module _2_digit_BCD_full_adder_with_7_segment_display (
  input  A,
  input  B,
  input  A_2,
  input  B_2
);

  wire _2_digit_BCD_full_adder_out_5, _2_digit_BCD_full_adder_out_6, _2_digit_BCD_full_adder_out_7,
       _7_segment_display_decoder_out_4, _7_segment_display_decoder_out_5, _7_segment_display_decoder_out_6,
       _7_segment_display_decoder_out_7, _7_segment_display_decoder_out_8, _7_segment_display_decoder_out_9,
       _7_segment_display_decoder_out_10;

  _2_digit_BCD_full_adder _2_digit_BCD_full_adder (
    .in_1(A), .in_2(B), .in_3(A_2), .in_4(B_2), .out_5(_2_digit_BCD_full_adder_out_5),
    .out_6(_2_digit_BCD_full_adder_out_6), .out_7(_2_digit_BCD_full_adder_out_7));
  main _7_segment_display_decoder (
    .S1(_2_digit_BCD_full_adder_out_5), .S2(_2_digit_BCD_full_adder_out_6),
    .C1(_2_digit_BCD_full_adder_out_7), .out_4(_7_segment_display_decoder_out_4),
    .out_5(_7_segment_display_decoder_out_5), .out_6(_7_segment_display_decoder_out_6),
    .out_7(_7_segment_display_decoder_out_7), .out_8(_7_segment_display_decoder_out_8),
    .out_9(_7_segment_display_decoder_out_9), .out_10(_7_segment_display_decoder_out_10));
  _7_Segment_Display_part u_7_segment_display_1 (
    .g(_7_segment_display_decoder_out_10), .f(_7_segment_display_decoder_out_9),
    .a(_7_segment_display_decoder_out_4), .b(_7_segment_display_decoder_out_5),
    .e(_7_segment_display_decoder_out_8), .d(_7_segment_display_decoder_out_7),
    .c(_7_segment_display_decoder_out_6), .dp(1'b0));
endmodule

module _2_digit_BCD_full_adder (
  input  in_1,
  input  in_2,
  input  in_3,
  input  in_4,
  output out_5,
  output out_6,
  output out_7
);

  wire and_1_out, and_2_out, and_3_out, xor_2_out;

  xor xor_1 (out_5, in_1, in_2);
  and and_1 (and_1_out, in_1, in_2);
  xor xor_2 (xor_2_out, in_3, in_4);
  xor xor_3 (out_6, xor_2_out, and_1_out);
  and and_2 (and_2_out, and_1_out, xor_2_out);
  and and_3 (and_3_out, in_4, in_3);
  or or_1 (out_7, and_2_out, and_3_out);
endmodule

module _2_DIGIT_BCD_FULL_ADDER (
  input  A,
  input  B,
  input  A_2,
  input  B_2,
  output out_5,
  output out_6,
  output out_7
);

  _2_digit_BCD_full_adder u_2_digit_bcd_full_adder_1 (
    .in_1(A), .in_2(B), .in_3(A_2), .in_4(B_2), .out_5(out_5), .out_6(out_6), .out_7(out_7));
endmodule
